# Fritzing sketch halloween-pumpkin-fire (saved by Fritzing 0.9.3b)
breadboards: 1

parts:
  WeMos_D1_Mini1 = WeMos D1 Mini
  J1 = Basic Servo
  PIR1 = PIR sensor
  Squix1 = OLED 0.96" 128x64 I2C SSD1306
  PIR2 = PIR sensor

nets:
  3V3: WeMos_D1_Mini1.3V3, Squix1.VCC
  VDD: WeMos_D1_Mini1.5V, J1.vcc, PIR1.VDD, PIR2.VDD
  N1: WeMos_D1_Mini1.D0, PIR1.SIG
  N2: WeMos_D1_Mini1.D1, Squix1.SCL
  N3: WeMos_D1_Mini1.D2, Squix1.SCA
  N4: WeMos_D1_Mini1.D5, PIR2.SIG
  N5: WeMos_D1_Mini1.D8, J1.pulse
  GND: WeMos_D1_Mini1.G, J1.gnd, PIR1.GND, Squix1.GND, PIR2.GND

custom parts:
  WeMos D1 Mini: The D1 mini is a mini wifi board based on ESP-8266EX.
